// Logisim project t888.circ as structural Verilog: 2 circuits, main circuit t888
module t888 (
  input  [7:0] in_1,
  output out_2,
  output out_3,
  output [7:0] out_4
);

  wire adder_1_cout, and_1_out, and_2_out, and_3_out, buffer_1_out, buffer_2_out, comparator_1_gt,
       comparator_2_eq, d_ff_1_q, multiplexer_4_out, multiplexer_5_out, multiplexer_7_out, nor_1_out,
       not_1_out, not_2_out, not_3_out, not_4_out, not_6_out, or_1_out, or_3_out, PC_p4, subtractor_1_bout,
       subtractor_2_bout;
  wire [1:0] comparator_3_eq, demultiplexer_1_out0, plarom_1_p1, plarom_1_p3, plarom_1_p3_3, plarom_1_p3_4;
  wire [3:0] multiplexer_3_out, PC_p5, PC_p5_2, RP_q;
  wire [7:0] adder_1_out, adder_2_out, and_6_out, IR_q, multiplexer_1_out, multiplexer_2_out,
       multiplexer_6_out, negator_1_out, not_5_out, or_4_out, plarom_1_p2, pull_resistor_1_node,
       register_3_q, result_q, ROM88_data, subtractor_1_out, subtractor_2_out, subtractor_3_out, xor_3_out;
  wire [7:7] and_7_out;
  wire [8:2] plarom_1_p3_2;
  wire [10:0] clock_1_out;

  Clock clock_1 (.out(clock_1_out[0]));
  // PlaRom #(.\and (16), .outputs(12), .Contents("0 0 2 0*7 2 0 0 2*4 0*4 1 0 2 1 2 0*9 1 1 2 2 0*7 1 1 2 1 0*7 1*3 2 0*7 1*3 2 2 0*6 1*3 2 1 2*3 1 0 0 1*4 2 0*4 2 0 1*5 2 0*5 1*6 2 0*4 1*6 2 2 0*3 1*7 2 0*12 1 0 1*5 2 0*5 1*3 2 2 1 2 2 0 0*6 1 0 1 0*7 1 0 0 1 0*8 1 0*5 1 1 0*4 1 0*5 1 1 0*4 1 1 0*9 1 0*7 1 0*9 1 0*6 1 0 0 1 0*6 1 1 0*12 1 0*5 1 0 0 1 0 0 1 0*7 1 0*15 1 0*5 1 0*24 1 0*4 1 0*7")) plarom_1: pin names not known; wires that end beside it: plarom_1_p1, plarom_1_p2, {plarom_1_p3_4, multiplexer_3_out[3], plarom_1_p3_2[8:5], plarom_1_p3_3, plarom_1_p3_2[2], plarom_1_p3}, clock_1_out[0]
  Pull_Resistor pull_resistor_1 (.node(pull_resistor_1_node));
  Register #(.Select("low")) IR (.D(ROM88_data), .Q(IR_q), .clk(clock_1_out[0]));  // open: en, clr
  Register #(.width(4), .Select("low")) RP (
    .D(IR_q[3:0]), .en(plarom_1_p3_2[6]), .Q(RP_q), .clk(clock_1_out[0]));  // open: clr
  and and_1 (and_1_out, plarom_1_p3[0], clock_1_out[0]);
  and and_2 (and_2_out, clock_1_out[0], plarom_1_p3[1]);
  // Probe on pull_resistor_1_node
  // Probe on pull_resistor_1_node
  Multiplexer #(.width(8), .disabled(0), .enable("false")) multiplexer_1 (
    .in0(ROM88_data), .in1({RP_q, IR_q[3:0]}), .out(multiplexer_1_out), .sel(plarom_1_p3_2[5]));
  not not_1 (not_1_out, not_2_out);
  Multiplexer #(.width(8), .enable("false")) multiplexer_2 (
    .in0(ROM88_data), .in1({PC_p5_2, IR_q[3:0]}), .out(multiplexer_2_out), .sel(buffer_1_out));
  not not_2 (not_2_out, buffer_2_out);
  buf buffer_1 (buffer_1_out, and_1_out);
  buf buffer_2 (buffer_2_out, and_2_out);
  nor nor_1 (nor_1_out, ~or_1_out, not_3_out, clock_1_out[0]);  // NOR_Gate
  not not_3 (not_3_out, clock_1_out[0]);
  or or_1 (or_1_out, and_1_out, and_2_out);
  // Probe on plarom_1_p2
  xor xor_1 (clock_1_out[10], multiplexer_4_out, IR_q[0]);
  Multiplexer #(.width(3), .enable("false")) multiplexer_3 (
    .in0(IR_q[6:4]), .in1(IR_q[2:0]), .out(multiplexer_3_out[2:0]), .sel(plarom_1_p3_2[8]));
  // Probe on plarom_1_p2
  Register #(.trigger("high"), .Select("low")) register_1 (
    .D(multiplexer_1_out), .Q(plarom_1_p2), .clk(clock_1_out[0]));  // open: en, clr
  Comparator #(.mode("unsigned")) comparator_1 (.a(plarom_1_p2), .b(8'hf7), .gt(comparator_1_gt));  // open: eq, lt
  Demultiplexer #(.width(2), .enable("false")) demultiplexer_1 (
    .out0(demultiplexer_1_out0), .out1(plarom_1_p1), .in(plarom_1_p3_3), .sel(comparator_1_gt));
  // Counter PC: pin names not known; wires that end beside it: not_1_out, multiplexer_2_out, not_2_out, PC_p4, {PC_p5_2, PC_p5}
  or or_2 (PC_p4, nor_1_out, clock_1_out[0]);
  Multiplexer #(.enable("false")) multiplexer_4 (
    .in0(comparator_3_eq[0]), .in1(comparator_3_eq[1]), .out(multiplexer_4_out), .sel(IR_q[1]));
  Comparator comparator_2 (.a(plarom_1_p2), .b({8{1'b1}}), .eq(comparator_2_eq));  // open: gt, lt
  Multiplexer #(.enable("false")) multiplexer_5 (
    .in0(comparator_3_eq[0]), .in1(comparator_3_eq[1]), .out(multiplexer_5_out), .sel(IR_q[5]));
  xor xor_2 (clock_1_out[9], multiplexer_5_out, IR_q[4]);
  or or_3 (or_3_out, demultiplexer_1_out0[1], demultiplexer_1_out0[0]);
  and and_3 (and_3_out, plarom_1_p3_2[2], clock_1_out[0]);
  ROM #(.Select("low")) ROM88 (.addr({PC_p5_2, PC_p5}), .data(ROM88_data));
  assign pull_resistor_1_node = and_3_out ? ROM88_data : 8'bz;  // Controlled_Buffer controlled_buffer_1
  assign pull_resistor_1_node = out_2 ? in_1 : 8'bz;  // Controlled_Buffer controlled_buffer_2
  and and_4 (out_2, plarom_1_p1[0], comparator_2_eq);
  and and_5 (out_3, comparator_2_eq, plarom_1_p1[1]);
  not not_4 (not_4_out, plarom_1_p3_2[7]);
  RAM #(.Select("high")) RAM88 (
    .addr(plarom_1_p2), .data(pull_resistor_1_node), .sel(or_3_out), .clk(clock_1_out[0]),
    .ld(demultiplexer_1_out0[0]));  // open: clr
  Register #(.trigger("low"), .Select("low")) register_2 (
    .D(pull_resistor_1_node), .en(out_3), .Q(out_4), .clk(clock_1_out[0]));  // open: clr
  Register #(.Select("low")) result (
    .D(pull_resistor_1_node), .en(not_4_out), .Q(result_q), .clk(clock_1_out[0]));  // open: clr
  Register #(.trigger("high"), .Select("low")) register_3 (
    .D(pull_resistor_1_node), .Q(register_3_q), .clk(clock_1_out[0]));  // open: en, clr
  Comparator comparator_3 (.a({8{1'b0}}), .b(result_q), .eq(comparator_3_eq[0]));  // open: gt, lt
  Adder adder_1 (.a(result_q), .b(register_3_q), .out(adder_1_out), .cin(and_7_out[7]), .cout(adder_1_cout));
  Subtractor subtractor_1 (
    .a(result_q), .b(register_3_q), .out(subtractor_1_out), .bin(and_7_out[7]), .bout(subtractor_1_bout));
  Subtractor subtractor_2 (
    .a(result_q), .b(register_3_q), .out(subtractor_2_out), .bin(and_7_out[7]), .bout(subtractor_2_bout));
  assign and_6_out = result_q & register_3_q;  // AND_Gate and_6, 8 bits wide
  assign or_4_out = result_q | register_3_q;  // OR_Gate or_4, 8 bits wide
  assign xor_3_out = result_q ^ register_3_q;  // XOR_Gate xor_3, 8 bits wide
  Negator negator_1 (.in(result_q), .out(negator_1_out));
  Adder adder_2 (.a(result_q), .b(8'h1), .out(adder_2_out));  // open: cin, cout
  Subtractor subtractor_3 (.a(result_q), .b(8'h1), .out(subtractor_3_out));  // open: bin, bout
  assign not_5_out = ~result_q;  // NOT_Gate not_5, 8 bits wide
  assign pull_resistor_1_node = ~clock_1_out[0] ? multiplexer_6_out : 8'bz;  // Controlled_Buffer controlled_buffer_3
  Multiplexer #(.select(4), .width(8), .enable("false")) multiplexer_6 (
    .in0(register_3_q), .in1(adder_1_out), .in2(subtractor_1_out), .in3(subtractor_2_out), .in4(and_6_out),
    .in5(or_4_out), .in6(xor_3_out), .in7(result_q), .in8(negator_1_out),
    .in9({result_q[6:0], and_7_out[7]}), .in10({and_7_out[7], result_q[7:1]}),
    .in11({{2{result_q[7]}}, result_q[6:1]}), .in12(adder_2_out), .in13(subtractor_3_out), .in14(not_5_out),
    .in15({8{1'b0}}), .out(multiplexer_6_out), .sel(multiplexer_3_out));
  not not_6 (not_6_out, multiplexer_3_out[2]);
  and and_7 (and_7_out[7], d_ff_1_q, comparator_3_eq[1]);
  Multiplexer #(.select(3)) multiplexer_7 (
    .in1(adder_1_cout), .in2(subtractor_1_bout), .in3(subtractor_2_bout), .in5(result_q[7]),
    .in6(result_q[0]), .in7(result_q[0]), .out(multiplexer_7_out),
    .sel({multiplexer_3_out[3], multiplexer_3_out[1:0]}), .en(not_6_out));  // open: in0, in4
  D_Flip_Flop #(.Pre_Clr_Positions("LEGACY"), .enable("true"), .NewFFLayout("false")) d_ff_1 (
    .clk(clock_1_out[0]), .D(plarom_1_p3_4[0]), .Q(d_ff_1_q), .en(plarom_1_p3_4[1]));  // open: Qn, preset, reset
  D_Flip_Flop #(.Pre_Clr_Positions("LEGACY"), .NewFFLayout("false")) d_ff_2 (
    .clk(clock_1_out[0]), .D(multiplexer_7_out), .Q(comparator_3_eq[1]));  // open: Qn, preset, reset

  // Notes on the sheet:
  //   On every rising edge of sysclock, latch Instr and increment PC.
  //   Additionally on falling edge of sysclock do PC op:
  //   00 Nothing
  //   01 Increment PC (skip data byte)
  //   10 Load PC from ROMdata (full jump/branch)
  //   11 Load least significant nibble of PC from Instr (near jump/branch)
  //   contents of ROM88 (hex, n*v repeats v):
  //   2f 18 20 ff ff ff 18 30 f0 18 a f1 80 ff c f0 81 d 5 b 18 41 f0 18 6 f1 80 ff c f0 81 d 5 19 18 a ff
  //   18 32 ff 18 30 ff 18 20 ff 18 20 ff c 1b 30 60 18 a ff 18 33 ff 18 30 ff 18 20 ff 18 30 ff c 1b 40
  //   63 18 a ff 18 34 ff 18 30 ff 18 20 ff 18 40 ff c 1b 50 66 18 a ff 18 35 ff 18 30 ff 18 20 ff 18 50
  //   ff c 1b 60 69 18 a ff 18 36 ff 18 30 ff 18 20 ff 18 60 ff c 1b 70 6 7c 18 a ff 18 37 ff 18 30 ff 18
  //   20 ff 18 70 ff c 1b 80 60 8f 1b 30 65
endmodule

module tes (
);

  wire clock_1_out, t888_1_out_3;
  wire [7:0] t888_1_out_4;

  t888 t888_1 (.out_3(t888_1_out_3), .out_4(t888_1_out_4));  // open: out_2, in_1
  // Probe on t888_1_out_4[6:0]
  Clock clock_1 (.out(clock_1_out));
  TTY #(.rows(7), .cols(19)) tty_1 (.data(t888_1_out_4[6:0]), .clk(clock_1_out), .we(t888_1_out_3));  // open: clr
endmodule
